# Fritzing sketch flowers (saved by Fritzing 0.9.2b)
circuit board: 7.60369cm x 7.5137cm

parts:
  Part1 = Arduino Uno (Rev3)
  J1 = Power Jack [package=power_jack_slot]
  T1 = TMP36 Temperature Sensor [thermistor_type=NTC part_number=DS18b20 package="TO92 [THT]"]
  Part2 = Real Time Clock Module - DS1307 RTC Breakout Board
  IC1 = L293D [package=THT]
  Part3 = Humidity Sensor - HIH-4030 Breakout
  Part4 = Humidity Sensor - HIH-4030 Breakout
  Part5 = Humidity Sensor - HIH-4030 Breakout
  M1 = DC Motor
  U1 = Voltage Regulator - Variable [package="TO220 [THT]"]
  KY-1 = Keyes Relay [package=THT]
  KY-2 = Keyes Relay [package=THT]
  Water_Level_Sensor1 = Water Level Sensor
  Reg1 = DC-DC CONVERTER [part_number=80633 package=dc-dc_converter]
  R1 = Resistor [tolerance=±5% resistance=4.7k package=THT]
  LCM1602_IIC1 = LCM1602 IIC [part_number="LCM1602 IIC" chip_label="LCM1602 IIC" package="DIP (Dual Inline) [THT]"]
  J3 = female pin header, 2 pins [form="♀ (female)"]
  J4 = female pin header, 2 pins [form="♀ (female)"]
  J5 = female pin header, 2 pins [form="♀ (female)"]
  J6 = female pin header, 3 pins [form="♀ (female)"]
  J7 = female pin header, 2 pins [form="♀ (female)"]
  J8 = female pin header, 2 pins [form="♀ (female)"]

nets (from the schematic view):
  N1: Part1.A0, Part4.OUT, J6.pin1
  N2: Part1.A1, Part3.OUT, J6.pin2
  N3: Part1.A2, Part5.OUT, J6.pin3
  N4: Part1.A3, Water_Level_Sensor1.SIG
  N5: Part1.A4/SDA, Part2.SDA, LCM1602_IIC1.SDA, J7.pin1
  N6: Part1.A5/SCL, Part2.SCL, LCM1602_IIC1.SCL, J7.pin2
  N7: Part1.D8, Water_Level_Sensor1.VCC
  GND: Part1.GND, T1.GND, Part2.GND, IC1.0V, IC1.In_2, IC1.In_3, KY-1.ground, KY-2.ground, Water_Level_Sensor1.GND, Reg1.OUT-, LCM1602_IIC1.GND, J5.pin1
  N8: Part1.D3_PWM, T1.Vout, R1.Pin_1
  N9: Part1.D4, IC1.Enable_2, J3.pin1
  N10: Part1.D5_PWM, IC1.Enable_1, J3.pin2
  N11: Part1.D6_PWM, KY-1.signal, J4.pin2
  N12: Part1.D7, KY-2.signal, J4.pin1
  N13: Part1.5V, T1.+Vs, R1.Pin_0
  VIN: Part1.VIN, J1.GND, J1.PWR, IC1.+Vmotor, Reg1.IN+, J5.pin2
  N14: J1.GNDBREAK, Reg1.IN-
  5V: Part2.5V, IC1.In_1, IC1.In_4, IC1.+V, KY-1.power, KY-2.power, Reg1.OUT+, LCM1602_IIC1.VCC
  N15: IC1.Out_1_(_Controlled_by_Enable_1_), M1.pin_2, J8.pin1
  N16: IC1.Out_2_(_Controlled_by_Enable_1_), M1.pin_1, J8.pin2
  GND_2: IC1.Out_3_(_Controlled_by_Enable_2_), Part3.GND, Part4.GND, Part5.GND, U1.OUT
  N17: IC1.Out_4_(_Controlled_by_Enable_2_), U1.ADJ
  VCC: Part3.VCC, Part4.VCC, Part5.VCC, U1.IN
  N18: LCM1602_IIC1.LED_A, LCM1602_IIC1.LED_B

notes:
  Light
  Pump

custom parts:
  Keyes Relay: The Keyes 5V relay module is suitable for SCM development, home appliance control. It uses a 5V~12V TIL control signal which can control DC / AC signal.
  Water Level Sensor: A water level sensor. This sensor operates at 3V to 5V. The Sig (signal) pin outputs an analogue signal that is in proportion to the amount of water in contact with the sensor.
  DC-DC CONVERTER: WYHP 5A constant current/voltage manufactured by Shenzhen Weiyapuhua Technology Co., Ltd
  LCM1602 IIC: I2C-Module to use a 1602 or 2004 LCD on with the wire.h libory Serial LCD Modul
